// Logisim project Proiect_calculator.circ as structural Verilog
module main (
  input  [7:0] A,
  input  [2:0] in_2,
  input  in_3,
  input  in_4,
  input  in_5,
  input  [7:0] B,
  output [7:0] out_7,
  output out_8,
  output out_9,
  output [7:0] out_10,
  output out_11,
  output [15:0] out_12,
  output [7:0] out_13,
  output out_14
);

  wire clock_1_out, clock_2_out;
  wire [2:0] control_unit_1_output;
  wire [6:0] hex_7seg_1_a_b_c_d_e_f_g, hex_7seg_2_a_b_c_d_e_f_g, hex_7seg_3_a_b_c_d_e_f_g,
       hex_7seg_4_a_b_c_d_e_f_g, hex_7seg_5_a_b_c_d_e_f_g, hex_7seg_6_a_b_c_d_e_f_g,
       hex_7seg_7_a_b_c_d_e_f_g, hex_7seg_8_a_b_c_d_e_f_g, hex_7seg_9_a_b_c_d_e_f_g,
       hex_7seg_10_a_b_c_d_e_f_g;
  wire [7:0] incarcator_a8biti_1_data_out, incarcator_b8biti_1_data_out;

  Clock clock_1 (.out(clock_1_out));
  Clock clock_2 (.out(clock_2_out));
  control_unit control_unit_1 (.Mode(in_2), .Reset(in_3), .Start(in_4), .Output(control_unit_1_output));
  Impartire impartire_1 (
    .clk(clock_1_out), .Reset(in_3), .Mode(control_unit_1_output), .A(incarcator_a8biti_1_data_out),
    .B(incarcator_b8biti_1_data_out), .Rezultat(out_13), .Done(out_14));
  hex_7seg hex_7seg_1 (.hex_in(out_13[3:0]), .a_b_c_d_e_f_g(hex_7seg_1_a_b_c_d_e_f_g));
  hex_7seg hex_7seg_2 (.hex_in(out_13[7:4]), .a_b_c_d_e_f_g(hex_7seg_2_a_b_c_d_e_f_g));
  incarcator_A8biti incarcator_a8biti_1 (
    .clk(clock_2_out), .reset(in_3), .mode(control_unit_1_output), .data_in(A),
    .data_out(incarcator_a8biti_1_data_out), .load(out_8));
  incarcator_B8biti incarcator_b8biti_1 (
    .clk(clock_2_out), .reset(in_3), .mode(control_unit_1_output), .data_in(B),
    .data_out(incarcator_b8biti_1_data_out), .load(out_11));
  hex_7seg hex_7seg_3 (.hex_in(out_12[3:0]), .a_b_c_d_e_f_g(hex_7seg_3_a_b_c_d_e_f_g));
  hex_7seg hex_7seg_4 (.hex_in(out_12[7:4]), .a_b_c_d_e_f_g(hex_7seg_4_a_b_c_d_e_f_g));
  hex_7seg hex_7seg_5 (.hex_in(out_12[11:8]), .a_b_c_d_e_f_g(hex_7seg_5_a_b_c_d_e_f_g));
  hex_7seg hex_7seg_6 (.hex_in(out_12[15:12]), .a_b_c_d_e_f_g(hex_7seg_6_a_b_c_d_e_f_g));
  _7_Segment_Display #(.active("false"), .decimalPoint("false")) u_7_segment_display_1 (
    .g(hex_7seg_2_a_b_c_d_e_f_g[0]), .f(hex_7seg_2_a_b_c_d_e_f_g[1]), .a(hex_7seg_2_a_b_c_d_e_f_g[6]),
    .b(hex_7seg_2_a_b_c_d_e_f_g[5]), .e(hex_7seg_2_a_b_c_d_e_f_g[2]), .d(hex_7seg_2_a_b_c_d_e_f_g[3]),
    .c(hex_7seg_2_a_b_c_d_e_f_g[4]));
  _7_Segment_Display #(.active("false"), .decimalPoint("false")) u_7_segment_display_2 (
    .g(hex_7seg_1_a_b_c_d_e_f_g[0]), .f(hex_7seg_1_a_b_c_d_e_f_g[1]), .a(hex_7seg_1_a_b_c_d_e_f_g[6]),
    .b(hex_7seg_1_a_b_c_d_e_f_g[5]), .e(hex_7seg_1_a_b_c_d_e_f_g[2]), .d(hex_7seg_1_a_b_c_d_e_f_g[3]),
    .c(hex_7seg_1_a_b_c_d_e_f_g[4]));
  sumator_complet sumator_complet_1 (
    .A(incarcator_a8biti_1_data_out), .B(incarcator_b8biti_1_data_out), .Mode(control_unit_1_output),
    .Reset(in_3), .CarryIn(in_5), .Rezultat(out_7), .CarryOut(out_9));
  scazator scazator_1 (
    .A(incarcator_a8biti_1_data_out), .B(incarcator_b8biti_1_data_out), .Mode(control_unit_1_output),
    .Reset(in_3), .Rezultat(out_10));
  inmultitor inmultitor_1 (
    .A(incarcator_a8biti_1_data_out), .B(incarcator_b8biti_1_data_out), .Mode(control_unit_1_output),
    .Reset(in_3), .Rezultat(out_12));
  _7_Segment_Display #(.active("false"), .decimalPoint("false")) u_7_segment_display_3 (
    .g(hex_7seg_6_a_b_c_d_e_f_g[0]), .f(hex_7seg_6_a_b_c_d_e_f_g[1]), .a(hex_7seg_6_a_b_c_d_e_f_g[6]),
    .b(hex_7seg_6_a_b_c_d_e_f_g[5]), .e(hex_7seg_6_a_b_c_d_e_f_g[2]), .d(hex_7seg_6_a_b_c_d_e_f_g[3]),
    .c(hex_7seg_6_a_b_c_d_e_f_g[4]));
  hex_7seg hex_7seg_7 (.hex_in(out_7[3:0]), .a_b_c_d_e_f_g(hex_7seg_7_a_b_c_d_e_f_g));
  hex_7seg hex_7seg_8 (.hex_in(out_7[7:4]), .a_b_c_d_e_f_g(hex_7seg_8_a_b_c_d_e_f_g));
  _7_Segment_Display #(.active("false"), .decimalPoint("false")) u_7_segment_display_4 (
    .g(hex_7seg_5_a_b_c_d_e_f_g[0]), .f(hex_7seg_5_a_b_c_d_e_f_g[1]), .a(hex_7seg_5_a_b_c_d_e_f_g[6]),
    .b(hex_7seg_5_a_b_c_d_e_f_g[5]), .e(hex_7seg_5_a_b_c_d_e_f_g[2]), .d(hex_7seg_5_a_b_c_d_e_f_g[3]),
    .c(hex_7seg_5_a_b_c_d_e_f_g[4]));
  _7_Segment_Display #(.active("false"), .decimalPoint("false")) u_7_segment_display_5 (
    .g(hex_7seg_4_a_b_c_d_e_f_g[0]), .f(hex_7seg_4_a_b_c_d_e_f_g[1]), .a(hex_7seg_4_a_b_c_d_e_f_g[6]),
    .b(hex_7seg_4_a_b_c_d_e_f_g[5]), .e(hex_7seg_4_a_b_c_d_e_f_g[2]), .d(hex_7seg_4_a_b_c_d_e_f_g[3]),
    .c(hex_7seg_4_a_b_c_d_e_f_g[4]));
  hex_7seg hex_7seg_9 (.hex_in(out_10[3:0]), .a_b_c_d_e_f_g(hex_7seg_9_a_b_c_d_e_f_g));
  hex_7seg hex_7seg_10 (.hex_in(out_10[7:4]), .a_b_c_d_e_f_g(hex_7seg_10_a_b_c_d_e_f_g));
  _7_Segment_Display #(.active("false"), .decimalPoint("false")) u_7_segment_display_6 (
    .g(hex_7seg_3_a_b_c_d_e_f_g[0]), .f(hex_7seg_3_a_b_c_d_e_f_g[1]), .a(hex_7seg_3_a_b_c_d_e_f_g[6]),
    .b(hex_7seg_3_a_b_c_d_e_f_g[5]), .e(hex_7seg_3_a_b_c_d_e_f_g[2]), .d(hex_7seg_3_a_b_c_d_e_f_g[3]),
    .c(hex_7seg_3_a_b_c_d_e_f_g[4]));
  _7_Segment_Display #(.active("false"), .decimalPoint("false")) u_7_segment_display_7 (
    .g(hex_7seg_8_a_b_c_d_e_f_g[0]), .f(hex_7seg_8_a_b_c_d_e_f_g[1]), .a(hex_7seg_8_a_b_c_d_e_f_g[6]),
    .b(hex_7seg_8_a_b_c_d_e_f_g[5]), .e(hex_7seg_8_a_b_c_d_e_f_g[2]), .d(hex_7seg_8_a_b_c_d_e_f_g[3]),
    .c(hex_7seg_8_a_b_c_d_e_f_g[4]));
  _7_Segment_Display #(.active("false"), .decimalPoint("false")) u_7_segment_display_8 (
    .g(hex_7seg_7_a_b_c_d_e_f_g[0]), .f(hex_7seg_7_a_b_c_d_e_f_g[1]), .a(hex_7seg_7_a_b_c_d_e_f_g[6]),
    .b(hex_7seg_7_a_b_c_d_e_f_g[5]), .e(hex_7seg_7_a_b_c_d_e_f_g[2]), .d(hex_7seg_7_a_b_c_d_e_f_g[3]),
    .c(hex_7seg_7_a_b_c_d_e_f_g[4]));
  _7_Segment_Display #(.active("false"), .decimalPoint("false")) u_7_segment_display_9 (
    .g(hex_7seg_10_a_b_c_d_e_f_g[0]), .f(hex_7seg_10_a_b_c_d_e_f_g[1]), .a(hex_7seg_10_a_b_c_d_e_f_g[6]),
    .b(hex_7seg_10_a_b_c_d_e_f_g[5]), .e(hex_7seg_10_a_b_c_d_e_f_g[2]), .d(hex_7seg_10_a_b_c_d_e_f_g[3]),
    .c(hex_7seg_10_a_b_c_d_e_f_g[4]));
  _7_Segment_Display #(.active("false"), .decimalPoint("false")) u_7_segment_display_10 (
    .g(hex_7seg_9_a_b_c_d_e_f_g[0]), .f(hex_7seg_9_a_b_c_d_e_f_g[1]), .a(hex_7seg_9_a_b_c_d_e_f_g[6]),
    .b(hex_7seg_9_a_b_c_d_e_f_g[5]), .e(hex_7seg_9_a_b_c_d_e_f_g[2]), .d(hex_7seg_9_a_b_c_d_e_f_g[3]),
    .c(hex_7seg_9_a_b_c_d_e_f_g[4]));
endmodule

// VHDL entity control_unit, as the project stores it:
library IEEE;
use IEEE.STD_LOGIC_1164.ALL;
entity control_unit is
    Port ( Mode : in std_logic_vector(2 downto 0);
           Reset : in std_logic;
           Start : in std_logic;
           Output : out std_logic_vector(2 downto 0));
end control_unit;
architecture Behavioral of control_unit is
begin
    process (Mode, Reset, Start)
    begin
        if Reset = '1' then
            Output <= "000"; 
        elsif Start = '1' then
            case Mode is
                when "001" =>
                    Output <= "001"; --adunare
                when "010" =>
                    Output <= "010"; --scadere
                when "011" =>
                    Output <= "011"; --inmultire
                when "100" =>
                    Output <= "100";  --impartire
                when "101" =>
                    Output <= "101";  	
                when "110" =>
                    Output <= "110"; 	
                when "111" =>
                    Output <= "111"; 
                when others =>
                    Output <= "000"; 
            end case;
        end if;
    end process;

end Behavioral;

// VHDL entity sumator_complet, as the project stores it:
library IEEE;
use IEEE.STD_LOGIC_1164.ALL;

entity sumator_complet is
    port(
        A, B: in std_logic_vector(7 downto 0);
        Mode: in std_logic_vector(2 downto 0);
        Reset: in std_logic;
        CarryIn: in std_logic;
        Rezultat: out std_logic_vector(7 downto 0);
        CarryOut: out std_logic
    );
end sumator_complet;

architecture behavioral of sumator_complet is
begin
    process(Reset, A, B, Mode, CarryIn)
        variable carry: std_logic := CarryIn;
    begin
        if Reset = '1' then
            Rezultat <= (others => '0');
            carry := '0';
        elsif mode = "001" then
            for i in 0 to 7 loop
                Rezultat(i) <= A(i) xor B(i) xor carry;
                carry := (A(i) and B(i)) or (A(i) and carry) or (B(i) and carry);
            end loop;
        else
            Rezultat <= (others => '0');
            carry := '0';
        end if;
        
        CarryOut <= carry;
    end process;
end behavioral;

// VHDL entity scazator, as the project stores it:
library IEEE;
use IEEE.STD_LOGIC_1164.ALL;
use IEEE.numeric_std.all; 
entity scazator is
    Port ( A : in std_logic_vector(7 downto 0);
           B : in std_logic_vector(7 downto 0);
           Mode : in std_logic_vector(2 downto 0);
           Reset : in std_logic;
           Rezultat : out std_logic_vector(7 downto 0));
end scazator;

architecture Behavioral of scazator is
begin

    process (A, B, Mode, Reset)
    begin
        if Reset = '1' then
            Rezultat <= (others => '0');
        elsif Mode = "010" then 
            Rezultat <= std_logic_vector(unsigned(A) + (not unsigned(B) + 1));
        else
            Rezultat <= (others => '0'); 
        end if;
    end process;

end Behavioral;

// VHDL entity inmultitor, as the project stores it:
library ieee;
use ieee.std_logic_1164.all;
use ieee.numeric_std.all;

entity inmultitor is
    port (
        A : in std_logic_vector(7 downto 0);
        B : in std_logic_vector(7 downto 0);
        Mode : in std_logic_vector(2 downto 0);
        Reset : in std_logic;
        Rezultat : out std_logic_vector(15 downto 0)
    );
end inmultitor;

architecture Behavioral of inmultitor is
begin
    process (Reset, A, B, Mode)
        variable tmp_p : std_logic_vector(15 downto 0) := (others => '0');
    begin
        if Reset = '1' then 
            tmp_p := (others => '0');
        elsif Mode = "011" then 
            tmp_p := (others => '0');
            for i in 0 to 7 loop
                if B(i) = '1' then
                    tmp_p := std_logic_vector(unsigned(tmp_p) + shift_left(unsigned(A), i));
                end if;
            end loop;
        else 
            tmp_p := (others => '0');
        end if;
        Rezultat <= tmp_p;
    end process;
end Behavioral;

// VHDL entity incarcator_A8biti, as the project stores it:
library ieee;
use ieee.std_logic_1164.all;
entity incarcator_A8biti is
    port (
        clk : in std_logic;        
        reset : in std_logic;      
        mode : in std_logic_vector(2 downto 0); 
        data_in : in std_logic_vector(7 downto 0); 
        data_out : out std_logic_vector(7 downto 0); 
        load : out std_logic
    );
end incarcator_A8biti;

architecture Behavioral of incarcator_A8biti is
    signal numar : std_logic_vector(7 downto 0); 
begin
    process(clk, reset)
    begin
        if reset = '1' then
            numar <= (others => '0'); 
            load <= '0'; 
        elsif rising_edge(clk) then
            if mode = "110" then 
                numar <= data_in; 
                load <= '1'; 
            else
                load <= '0'; 
            end if;
        end if;
    end process;
    data_out <= numar; 
end Behavioral;

// VHDL entity incarcator_B8biti, as the project stores it:
library ieee;
use ieee.std_logic_1164.all;
entity incarcator_B8biti is
    port (
        clk : in std_logic;        
        reset : in std_logic;     
        mode : in std_logic_vector(2 downto 0); 
        data_in : in std_logic_vector(7 downto 0); 
        data_out : out std_logic_vector(7 downto 0); 
        load : out std_logic       
    );
end incarcator_B8biti;
architecture Behavioral of incarcator_B8biti is
    signal numar : std_logic_vector(7 downto 0); 
begin
    process(clk,reset)
    begin
        if reset = '1' then
            numar <= (others => '0'); 
            load <= '0'; 
        elsif rising_edge(clk) then
            if mode = "110" then 
                numar <= data_in;
                load <= '1'; 
            else
                load <= '0'; 
            end if;
        end if;
    end process;

    data_out <= numar; 
end Behavioral;

// VHDL entity hex_7seg, as the project stores it:
LIBRARY ieee;
USE ieee.std_logic_1164.all;

ENTITY hex_7seg IS

  PORT (
 hex_in: in std_logic_vector(3 downto 0);
  		a_b_c_d_e_f_g: out std_logic_vector(6 downto 0));

END hex_7seg;

ARCHITECTURE TypeArchitecture OF hex_7seg IS

BEGIN

	a_b_c_d_e_f_g <= "0000001" when hex_in= x"0" else
				  "1001111" when hex_in= x"1" else
				  "0010010" when hex_in= x"2" else
				  "0000110" when hex_in= x"3" else
				  "1001100" when hex_in= x"4" else
				  "0100100" when hex_in= x"5" else
				  "0100000" when hex_in= x"6" else
				  "0001111" when hex_in= x"7" else
				  "0000000" when hex_in= x"8" else
				  "0000100" when hex_in= x"9" else
				  "0001000" when hex_in= x"A" else
				  "1100000" when hex_in= x"B" else
				  "0110001" when hex_in= x"C" else
				  "1000010" when hex_in= x"d" else
				  "0110000" when hex_in= x"E" else
				  "0111000" when hex_in= x"F" else
				  "1111111";

END TypeArchitecture;

// VHDL entity Scazator2, as the project stores it:
library ieee;
use ieee.std_logic_1164.all;
use ieee.numeric_std.all;

entity Scazator2 is
    port (
        A, B: in std_logic_vector(7 downto 0);
        Mode: in std_logic_vector(2 downto 0);
        Rezultat: out std_logic_vector(7 downto 0);
        Reset: in std_logic
    );
end Scazator2;

architecture Behavioral of Scazator2 is
begin
    process(a, b, mode, reset)
        variable temp: unsigned(7 downto 0);
    begin
        if reset = '1' then
            Rezultat <= (others => '0');
        elsif mode = "100" then
            temp := unsigned(a);
            
            for i in 0 to 7 loop
                if temp(i) = '1' and b(i) = '0' then
                    Rezultat(i) <= '1';
                elsif temp(i) = '0' and b(i) = '1' then
                    Rezultat(i) <= '1';
                    temp(i+1 downto 0) := temp(i+1 downto 0) - unsigned(b(i+1 downto 0));
                else
                    Rezultat(i) <= '0';
                end if;
            end loop;
        else
            Rezultat <= (others => '0');
        end if;
    end process;
end Behavioral;

// VHDL entity Impartire, as the project stores it:
library IEEE;
use IEEE.STD_LOGIC_1164.ALL;
use IEEE.NUMERIC_STD.ALL;

entity Impartire is
    Port (
        clk    : in  std_logic;
        Reset  : in  std_logic;
        Mode   : in  std_logic_vector(2 downto 0);
        A      : in  std_logic_vector(7 downto 0);
        B      : in  std_logic_vector(7 downto 0);
        Rezultat      : out std_logic_vector(7 downto 0);
        Done   : out std_logic
    );
end Impartire;

architecture Behavioral of Impartire is
    function divide(a: unsigned; b: unsigned) return unsigned is
        variable a1 : unsigned(a'length-1 downto 0) := a;
        variable b1 : unsigned(b'length-1 downto 0) := b;
        variable p1 : unsigned(b'length downto 0) := (others => '0');
        variable i : integer := 0;
    begin
        for i in 0 to b'length-1 loop
            p1(b'length-1 downto 1) := p1(b'length-2 downto 0);
            p1(0) := a1(a'length-1);
            a1(a'length-1 downto 1) := a1(a'length-2 downto 0);
            p1 := p1 - b1;
            if p1(b'length-1) = '1' then
                a1(0) := '0';
                p1 := p1 + b1;
            else
                a1(0) := '1';
            end if;
        end loop;
        return a1;
    end divide;
    signal dividend_reg : unsigned(7 downto 0);
    signal divisor_reg  : unsigned(7 downto 0);
    signal quotient_reg : unsigned(7 downto 0);
    signal done_reg     : std_logic;

begin
    process (clk)
    begin
        if rising_edge(clk) then
            if reset = '1' then
                dividend_reg <= (others => '0');
                divisor_reg <= (others => '0');
                quotient_reg <= (others => '0');
                done_reg <= '0';
            else
                if Mode = "100" then
                    dividend_reg <= unsigned(A);
                    divisor_reg <= unsigned(B);
                    quotient_reg <= divide(dividend_reg, divisor_reg);
                    done_reg <= '1';
                else
                    done_reg <= '0';
                end if;
            end if;
        end if;
    end process;
     Rezultat<= std_logic_vector(quotient_reg);
    	Done <= done_reg;
end Behavioral;
